# Fritzing sketch Complete_thermocycler (saved by Fritzing 0.9.3b)
breadboards: 1

parts:
  Q1 = Basic FET N-Channel [package="TO220 [THT]"]
  Q3 = Basic FET N-Channel [package="TO220 [THT]"]
  DS2 = DS18B20 1-Wire Temperature Sensor [part_number=DS18B20]
  R3 = Rotary Potentiometer (Small) [maximum_resistance=100kΩ package=THT]
  S3 = Pushbutton [package="[THT]"]
  Q2 = Basic FET N-Channel [package="TO220 [THT]"]
  R7 = Resistor [tolerance=±5% resistance=10k package=THT]
  R8 = Resistor [tolerance=±5% resistance=10k package=THT]
  R9 = Resistor [tolerance=±5% resistance=10k package=THT]
  D1 = Rectifier Diode [part_number=1N4001 package="Melf DO-213 AB [SMD]"]
  DS3 = DS18B20 1-Wire Temperature Sensor [part_number=DS18B20]
  M4 = DC Motor
  J4 = Power Jack [package=power_jack_smd]
  U3 = SWITCH-SPST-2 [package=r_sw_th]
  LCM1602_IIC3 = LCM1602 IIC [part_number="LCM1602 IIC" chip_label="LCM1602 IIC" package="DIP (Dual Inline) [THT]"]
  LCD2 = LCD screen
  R15 = Resistor [tolerance=±5% resistance=4.7k package=THT]
  R16 = Resistor [tolerance=±5% resistance=6.8 package="2512 [SMD]"]
  R17 = Resistor [tolerance=±5% resistance=6.8 package="2512 [SMD]"]
  R18 = Resistor [tolerance=±5% resistance=4.7k package=THT]
  R19 = Resistor [tolerance=±5% resistance=10k package=THT]
  Part2 = Arduino Leonardo (Rev3b)

nets:
  N1: Q1.gate, R7.Pin_1, Part2.D7
  N2: Q1.drain, R17.Pin_1
  GND: Q1.source, Q3.source, DS2.GND, R3.wiper, Q2.source, R7.Pin_0, R8.Pin_0, R9.Pin_0, DS3.GND, J4.GNDBREAK, LCM1602_IIC3.GND, R19.Pin_1, Part2.GND
  N3: Q3.gate, R8.Pin_1, Part2.D6_PWM/A7
  N4: Q3.drain, R16.Pin_1
  VDD: DS2.VDD, S3.Pin_1, S3.Pin_2, DS3.VDD, LCM1602_IIC3.VCC, R15.Pin_1, R18.Pin_1, Part2.5V
  N5: DS2.DQ, R18.Pin_0, Part2.D10_PWM/A10
  N6: R3.leg1, Part2.D1/TX
  N7: R3.leg2, Part2.D0/RX
  N8: S3.Pin_3, S3.Pin_4, R19.Pin_0, Part2.D11_PWM
  N9: Q2.gate, R9.Pin_1, Part2.D5_PWM
  N10: Q2.drain, D1.anode
  N11: D1.cathode, M4.pin_1, U3.O, R16.Pin_0, R17.Pin_0, Part2.VIN
  N12: DS3.DQ, R15.Pin_0, Part2.D9_PWM/A9
  N13: J4.GND, U3.P
  VSS: LCM1602_IIC3.VSS, LCD2.VSS
  VDD_2: LCM1602_IIC3.VDD, LCD2.VDD
  N14: LCM1602_IIC3.V0, LCD2.V0
  N15: LCM1602_IIC3.RS, LCD2.RS
  N16: LCM1602_IIC3.RW, LCD2.R/W
  N17: LCM1602_IIC3.E, LCD2.E
  N18: LCM1602_IIC3.D0, LCD2.DB0
  N19: LCM1602_IIC3.D1, LCD2.DB1
  N20: LCM1602_IIC3.D2, LCD2.DB2
  N21: LCM1602_IIC3.D3, LCD2.DB3
  N22: LCM1602_IIC3.D4, LCD2.DB4
  N23: LCM1602_IIC3.D5, LCD2.DB5
  N24: LCM1602_IIC3.D6, LCD2.DB6
  N25: LCM1602_IIC3.D7, LCD2.DB7
  N26: LCM1602_IIC3.A, LCD2.LED+
  N27: LCM1602_IIC3.K, LCD2.LED-
  N28: LCM1602_IIC3.SDA, Part2.D2/SDA
  N29: LCM1602_IIC3.SCL, Part2.D3_PWM/SCL
  N30: LCM1602_IIC3.LED_A, LCM1602_IIC3.LED_B

notes:
  thermo sensors
  + 4.7K ohm R
  Ceramic resistors
  Fan
  12V power Supply
  Rotary encoder
  10K ohm R +
  Push Button
  Mosfets
  10K ohm R

custom parts:
  LCM1602 IIC: I2C-Module to use a 1602 or 2004 LCD on with the wire.h libory Serial LCD Modul
