# Fritzing sketch Thermocycler-Fritzing (saved by Fritzing 0.9.2b)
breadboards: 1

parts:
  Q1 = Basic FET N-Channel [package="TO220 [THT]"]
  Q3 = Basic FET N-Channel [package="TO220 [THT]"]
  R3 = Rotary Potentiometer (Small) [maximum_resistance=100kΩ package=THT]
  S3 = Pushbutton [package="[THT]"]
  Q2 = Basic FET N-Channel [package="TO220 [THT]"]
  R8 = Resistor [tolerance=±5% resistance=10k package=THT]
  R9 = Resistor [tolerance=±5% resistance=10k package=THT]
  D1 = Rectifier Diode [part_number=1N4001 package="Melf DO-213 AB [SMD]"]
  M4 = DC Motor
  J4 = Power Jack [package=power_jack_smd]
  U3 = SWITCH-SPST-2 [package=r_sw_th]
  LCM1602_IIC3 = LCM1602 IIC [part_number="LCM1602 IIC" chip_label="LCM1602 IIC" package="DIP (Dual Inline) [THT]"]
  LCD2 = LCD screen
  R15 = Resistor [tolerance=±5% resistance=10k package=THT]
  R16 = Resistor [tolerance=±5% resistance=6.8 package="2512 [SMD]"]
  R17 = Resistor [tolerance=±5% resistance=6.8 package="2512 [SMD]"]
  R18 = Resistor [tolerance=±5% resistance=10k package=THT]
  R19 = Resistor [tolerance=±5% resistance=10k package=THT]
  Part2 = Arduino Leonardo (Rev3b)
  R20 = Temperature Sensor (Thermistor) [thermistor_type=NTC package=THT]
  R21 = Temperature Sensor (Thermistor) [thermistor_type=NTC package=THT]
  R7 = Resistor [tolerance=±2% resistance=100k package=THT]

nets:
  N1: Q1.gate, Part2.D7, R7.Pin_1
  N2: Q1.drain, R17.Pin_1
  GND: Q1.source, Q3.source, R3.wiper, Q2.source, R8.Pin_0, R9.Pin_0, J4.GNDBREAK, LCM1602_IIC3.GND, R15.Pin_0, R18.Pin_0, R19.Pin_1, Part2.GND, R20.pin_0, R21.pin_0, R7.Pin_0
  N3: Q3.gate, R8.Pin_1, Part2.D6_PWM/A7
  N4: Q3.drain, R16.Pin_1
  N5: R3.leg1, Part2.D1/TX
  N6: R3.leg2, Part2.D0/RX
  VCC: S3.Pin_1, S3.Pin_2, LCM1602_IIC3.VCC, Part2.5V
  N7: S3.Pin_3, S3.Pin_4, R19.Pin_0, Part2.D11_PWM
  N8: Q2.gate, R9.Pin_1, Part2.D5_PWM
  N9: Q2.drain, D1.anode, M4.pin_2
  N10: D1.cathode, M4.pin_1, U3.O, R16.Pin_0, R17.Pin_0, Part2.VIN
  N11: J4.PWR, U3.P
  VSS: LCM1602_IIC3.VSS, LCD2.VSS
  VDD: LCM1602_IIC3.VDD, LCD2.VDD
  N12: LCM1602_IIC3.V0, LCD2.V0
  N13: LCM1602_IIC3.RS, LCD2.RS
  N14: LCM1602_IIC3.RW, LCD2.R/W
  N15: LCM1602_IIC3.E, LCD2.E
  N16: LCM1602_IIC3.D0, LCD2.DB0
  N17: LCM1602_IIC3.D1, LCD2.DB1
  N18: LCM1602_IIC3.D2, LCD2.DB2
  N19: LCM1602_IIC3.D3, LCD2.DB3
  N20: LCM1602_IIC3.D4, LCD2.DB4
  N21: LCM1602_IIC3.D5, LCD2.DB5
  N22: LCM1602_IIC3.D6, LCD2.DB6
  N23: LCM1602_IIC3.D7, LCD2.DB7
  N24: LCM1602_IIC3.A, LCD2.LED+
  N25: LCM1602_IIC3.K, LCD2.LED-
  N26: LCM1602_IIC3.SDA, Part2.D2/SDA
  N27: LCM1602_IIC3.SCL, Part2.D3_PWM/SCL
  N28: LCM1602_IIC3.LED_A, LCM1602_IIC3.LED_B
  N29: R15.Pin_1, Part2.A0, R21.pin_1
  N30: R18.Pin_1, Part2.A1, R20.pin_1

notes:
  Ceramic resistors
  Fan
  12V power Supply
  Rotary encoder
  10K Resistor +
  Push Button
  Mosfets
  10K Thermistors
  Switch

custom parts:
  LCM1602 IIC: I2C-Module to use a 1602 or 2004 LCD on with the wire.h libory Serial LCD Modul
